// Logisim project simple_register.circ as structural Verilog: 1 circuit, main circuit counter
module counter (
  input  [7:0] DATA_IN,
  input  CLK,
  input  RES,
  output [7:0] DATA_OUT
);

  D_Flip_Flop d_ff_1 (.clk(CLK), .D(DATA_IN[0]), .Q(DATA_OUT[0]), .en(RES));  // open: Qn, preset, reset
  D_Flip_Flop d_ff_2 (.clk(CLK), .D(DATA_IN[1]), .Q(DATA_OUT[1]), .en(RES));  // open: Qn, preset, reset
  D_Flip_Flop d_ff_3 (.clk(CLK), .D(DATA_IN[2]), .Q(DATA_OUT[2]), .en(RES));  // open: Qn, preset, reset
  D_Flip_Flop d_ff_4 (.clk(CLK), .D(DATA_IN[3]), .Q(DATA_OUT[3]), .en(RES));  // open: Qn, preset, reset
  D_Flip_Flop d_ff_5 (.clk(CLK), .D(DATA_IN[4]), .Q(DATA_OUT[4]), .en(RES));  // open: Qn, preset, reset
  D_Flip_Flop d_ff_6 (.clk(CLK), .D(DATA_IN[5]), .Q(DATA_OUT[5]), .en(RES));  // open: Qn, preset, reset
  D_Flip_Flop d_ff_7 (.clk(CLK), .D(DATA_IN[6]), .Q(DATA_OUT[6]), .en(RES));  // open: Qn, preset, reset
  D_Flip_Flop d_ff_8 (.clk(CLK), .D(DATA_IN[7]), .Q(DATA_OUT[7]), .en(RES));  // open: Qn, preset, reset
endmodule
