// Logisim project reg8.circ as structural Verilog: 2 circuits, main circuit reg8
module reg8 (
  input  clk,
  input  rW,
  input  [7:0] IN,
  input  shift,
  input  ROT,
  input  lR,
  input  [2:0] lop,
  output [7:0] OUT,
  output CARRY
);

  wire and_1_out, and_3_out, multiplexer_1_out;
  wire [1:1] and_2_out;

  and and_1 (and_1_out, ROT, CARRY);
  \cell  _0 (
    .q(and_1_out), .d(IN[0]), .qii(OUT[1]), .clk(clk), .op({lop, shift, ROT, lR, rW}), .qi(OUT[0]));  // open: nqi
  \cell  _4 (.q(OUT[3]), .d(IN[4]), .qii(OUT[5]), .clk(clk), .op({lop, shift, ROT, lR, rW}), .qi(OUT[4]));  // open: nqi
  \cell  _1 (.q(OUT[0]), .d(IN[1]), .qii(OUT[2]), .clk(clk), .op({lop, shift, ROT, lR, rW}), .qi(OUT[1]));  // open: nqi
  \cell  _5 (.q(OUT[4]), .d(IN[5]), .qii(OUT[6]), .clk(clk), .op({lop, shift, ROT, lR, rW}), .qi(OUT[5]));  // open: nqi
  and and_2 (and_2_out[1], rW, ROT);
  \cell  _2 (.q(OUT[1]), .d(IN[2]), .qii(OUT[3]), .clk(clk), .op({lop, shift, ROT, lR, rW}), .qi(OUT[2]));  // open: nqi
  \cell  _6 (.q(OUT[5]), .d(IN[6]), .qii(OUT[7]), .clk(clk), .op({lop, shift, ROT, lR, rW}), .qi(OUT[6]));  // open: nqi
  D_Flip_Flop u_carry (.clk(clk), .D(multiplexer_1_out), .Q(CARRY));  // open: Qn, preset, en, reset
  Multiplexer #(.select(2)) multiplexer_1 (
    .in0(CARRY), .in1(CARRY), .in2(OUT[7]), .in3(OUT[0]), .out(multiplexer_1_out), .sel({and_2_out[1], lR}));  // open: en
  \cell  _3 (.q(OUT[2]), .d(IN[3]), .qii(OUT[4]), .clk(clk), .op({lop, shift, ROT, lR, rW}), .qi(OUT[3]));  // open: nqi
  \cell  _7 (
    .q(OUT[6]), .d(IN[7]), .qii(and_3_out), .clk(clk), .op({lop, shift, ROT, lR, rW}), .qi(OUT[7]));  // open: nqi
  and and_3 (and_3_out, ROT, CARRY);

  // Other names for the same wires on the sheet: opcode[6:0] = {lop, shift, ROT, lR, rW}; Cout = CARRY; d0 = IN[0];
  //   d1 = IN[1]; d2 = IN[2]; d3 = IN[3]; d4 = IN[4]; d5 = IN[5]; d6 = IN[6]; d7 = IN[7]; q0 = OUT[0]; q1 = OUT[1];
  //   q2 = OUT[2]; q3 = OUT[3]; q4 = OUT[4]; q5 = OUT[5]; q6 = OUT[6]; q7 = OUT[7]

  // Notes on the sheet:
  //   Logical OPCODE
  //   0 - READ
  //   1 - WRITE
  //   2 - AND
  //   3 - OR
  //   4 - XOR
  //   5 - NAND
  //   6 - NOR
  //   7 - XNOR
endmodule

module \cell  (
  input  q,
  input  d,
  input  qii,
  input  clk,
  input  [6:0] op,
  output qi,
  output nqi
);

  wire and_1_out, multiplexer_1_out, multiplexer_2_out, multiplexer_3_out, multiplexer_4_out, not_1_out,
       not_2_out, not_3_out, not_4_out, not_5_out, or_1_out, Sl, xi, xor_1_out;

  xor xor_1 (xor_1_out, qi, d);
  and and_1 (and_1_out, qi, d);
  or or_1 (or_1_out, qi, d);
  not not_1 (not_1_out, Sl);
  Multiplexer multiplexer_1 (.in0(qi), .in1(d), .out(multiplexer_1_out), .sel(op[0]));  // open: en
  not not_2 (not_2_out, and_1_out);
  not not_3 (not_3_out, or_1_out);
  not not_4 (not_4_out, xor_1_out);
  Multiplexer #(.select(3)) multiplexer_2 (
    .in0(qi), .in1(d), .in2(q), .in3(qii), .in4(q), .in5(qii), .in6(d), .in7(qi), .out(multiplexer_2_out),
    .sel(op[3:1]), .en(Sl));
  or or_2 (Sl, op[3], op[2]);
  Multiplexer #(.select(3)) multiplexer_3 (
    .in0(multiplexer_1_out), .in1(multiplexer_1_out), .in2(and_1_out), .in3(or_1_out), .in4(xor_1_out),
    .in5(not_2_out), .in6(not_3_out), .in7(not_4_out), .out(multiplexer_3_out), .sel(op[6:4]), .en(not_1_out));
  D_Flip_Flop d_ff_1 (.clk(clk), .D(multiplexer_4_out), .Q(qi));  // open: Qn, preset, en, reset
  Multiplexer multiplexer_4 (.in0(qi), .in1(xi), .out(multiplexer_4_out), .sel(op[0]));  // open: en
  Multiplexer multiplexer_5 (.in0(multiplexer_2_out), .in1(multiplexer_3_out), .out(xi), .sel(not_5_out));  // open: en
  not not_5 (not_5_out, Sl);
  not not_6 (nqi, qi);

  // Other names for the same wires on the sheet: rW = op[0]; lR = op[1]; sop[2:0] = op[3:1]; r = op[2]; s = op[3];
  //   lop[2:0] = op[6:4]
endmodule
